# Fritzing sketch bow-stringless-bass 2 (saved by Fritzing 0.9.10b)
circuit board: 4.11778cm x 4.91439cm
breadboards: 1

parts:
  proto2 = Adafruit_PermaProto_1_4_Board
  S1 = Pushbutton [package="[THT]"]
  U1 = RJ45 Jack [package=rj45-8]
  Part2 = Adafruit FXOS8700 + FXAS21002 9 DoF Breakout [part_number="Adafruit #3463"]
  NEOPIXEL1 = Neopixel Strip -- Black (30/m) [part_number=1376]

nets:
  N1: proto2.connectorA1, U1.1, NEOPIXEL1.GND
  N2: proto2.connectorA2, U1.2, NEOPIXEL1.Din
  N3: proto2.connectorA3, U1.3, NEOPIXEL1.+5V
  N4: proto2.connectorA4, U1.4, Part2.VIN
  N5: proto2.connectorA5, S1.Pin_3, S1.Pin_4, U1.8
  N6: proto2.connectorA6, U1.7, Part2.SDA
  N7: proto2.connectorA7, U1.6, Part2.SCL
  N8: proto2.connectorA8, S1.Pin_1, S1.Pin_2, U1.5, Part2.GND
  N9: proto2.connectorB8, proto2.connectorB13
  N10: proto2.connectorE4, proto2.connectorF6
  N11: proto2.connectorE5, proto2.connectorF8
  N12: proto2.connectorE6, proto2.connectorF9
  N13: proto2.connectorE7, proto2.connectorF10
  N14: proto2.connectorI8, proto2.connectorI13

custom parts:
  Adafruit FXOS8700 + FXAS21002 9 DoF Breakout: The NXP Precision 9DoF breakout combines two of the best motion sensors we've tested here at Adafruit: The FXOS8700 3-Axis accelerometer and magnetometer, and the FXAS21002 3-axis gyroscope. These two sensors combine to make a nice 9-DoF kit, that can be used for motion and orientation sensing. In particular, we think this sensor set is ideal for AHRS-based orientation calculations: the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
  Neopixel Strip -- Black (30/m): These NeoPixel strips have 30 digitally-addressable pixel LEDs per meter and are very affordable and are only 12.5 mm wide, 10 mm if you remove the strip from the casing.
